// Logisim project Nawal Ayesha Khan_1911301042 Project.circ as structural Verilog: 4 circuits, main circuit main
module main (
);

  wire clock_1_out, counter_1_a0, counter_1_a1, counter_1_a2, mux_implementation_1_a_2,
       mux_implementation_1_b_2, mux_implementation_1_c_2, mux_implementation_1_d, mux_implementation_1_e,
       mux_implementation_1_f, mux_implementation_1_g;

  Clock clock_1 (.out(clock_1_out));
  Counter counter_1 (.A2(counter_1_a2), .A1(counter_1_a1), .A0(counter_1_a0), .in_1(clock_1_out));
  MUX_Implementation mux_implementation_1 (
    .A(counter_1_a2), .B(counter_1_a1), .C(counter_1_a0), .a_2(mux_implementation_1_a_2),
    .b_2(mux_implementation_1_b_2), .c_2(mux_implementation_1_c_2), .d(mux_implementation_1_d),
    .e(mux_implementation_1_e), .f(mux_implementation_1_f), .g(mux_implementation_1_g));
  _7_Segment_Display u_7_segment_display_1 (
    .g(mux_implementation_1_g), .f(mux_implementation_1_f), .a(mux_implementation_1_a_2),
    .b(mux_implementation_1_b_2), .e(mux_implementation_1_e), .d(mux_implementation_1_d),
    .c(mux_implementation_1_c_2));  // open: dp
endmodule

module _4_1_MUX (
  input  I3,
  input  I2,
  input  I1,
  input  I0,
  input  S1,
  input  S0,
  output F
);

  wire and_1_out, and_2_out, and_3_out, and_4_out, not_1_out, not_2_out;

  not not_1 (not_1_out, S0);
  not not_2 (not_2_out, S1);
  and and_1 (and_1_out, not_1_out, I0, not_2_out);
  and and_2 (and_2_out, S0, not_2_out, I1);
  and and_3 (and_3_out, not_1_out, S1, I2);
  and and_4 (and_4_out, S0, S1, I3);
  or or_1 (F, and_1_out, and_2_out, and_3_out, and_4_out);
endmodule

module MUX_Implementation (
  input  A,
  input  B,
  input  C,
  output a_2,
  output b_2,
  output c_2,
  output d,
  output e,
  output f,
  output g
);

  wire not_1_out;

  not not_1 (not_1_out, C);
  _4_1_MUX u_4_1_mux_1 (.F(a_2), .I3(C), .I2(1'b0), .I1(1'b0), .I0(1'b0), .S1(A), .S0(B));
  _4_1_MUX u_4_1_mux_2 (.F(b_2), .I3(not_1_out), .I2(C), .I1(1'b0), .I0(1'b0), .S1(A), .S0(B));
  _4_1_MUX u_4_1_mux_3 (.F(c_2), .I3(not_1_out), .I2(C), .I1(not_1_out), .I0(1'b0), .S1(A), .S0(B));
  _4_1_MUX u_4_1_mux_4 (.F(d), .I3(1'b1), .I2(1'b1), .I1(C), .I0(1'b0), .S1(A), .S0(B));
  _4_1_MUX u_4_1_mux_5 (.F(e), .I3(1'b1), .I2(1'b1), .I1(1'b1), .I0(C), .S1(A), .S0(B));
  _4_1_MUX u_4_1_mux_6 (.F(f), .I3(C), .I2(1'b1), .I1(1'b0), .I0(C), .S1(A), .S0(B));
  _4_1_MUX u_4_1_mux_7 (.F(g), .I3(1'b1), .I2(1'b0), .I1(1'b1), .I0(1'b0), .S1(A), .S0(B));

  // Notes on the sheet:
  //   0
  //   C
  //   C'
  //   C
  //   1
  //   1
  //   1
  //   C
  //   C
  //   1
  //   0
  //   1
  //   0
  //   0
  //   0
  //   C
  //   0
  //   0
  //   C'
  //   C
  //   C'
  //   0
  //   C
  //   1
  //   1
  //   0
  //   1
  //   C
  //   a
  //   b
  //   c
  //   d
  //   e
  //   f
  //   g
endmodule

module Counter (
  input  in_1,
  output A2,
  output A1,
  output A0
);

  wire and_1_out;

  and and_1 (and_1_out, A0, A1);
  T_Flip_Flop t_ff_1 (.clk(in_1), .T(and_1_out), .Q(A2));  // open: Qn, preset, reset, en
  T_Flip_Flop t_ff_2 (.clk(in_1), .T(A0), .Q(A1));  // open: Qn, preset, reset, en
  T_Flip_Flop t_ff_3 (.clk(in_1), .T(1'b1), .Q(A0));  // open: Qn, preset, reset, en
endmodule
