// Logisim project Nawal Ayesha_1911301042 Final.circ as structural Verilog
module IC_7404_NOT (
  input  GND_7,
  input  _1,
  input  _3,
  input  _5,
  input  _9,
  input  _11,
  input  _13,
  input  VCC_14,
  output _2,
  output _4,
  output _6,
  output _8,
  output _10,
  output _12
);

  not not_1 (_2, _1);
  not not_2 (_4, _3);
  not not_3 (_6, _5);
  not not_4 (_8, _9);
  not not_5 (_10, _11);
  not not_6 (_12, _13);
endmodule

module IC_7408_AND (
  input  VCC_14,
  input  _1,
  input  _2,
  input  _4,
  input  _5,
  input  _9,
  input  _10,
  input  _12,
  input  _13,
  input  GND_7,
  output _3,
  output _6,
  output _8,
  output _11
);

  and and_1 (_3, _1, _2);
  and and_2 (_6, _4, _5);
  and and_3 (_8, _9, _10);
  and and_4 (_11, _12, _13);
endmodule

module IC_7432_OR (
  input  VCC_14,
  input  _1,
  input  _2,
  input  _4,
  input  _5,
  input  _9,
  input  _10,
  input  _12,
  input  _13,
  input  GND_7,
  output _3,
  output _6,
  output _8,
  output _11
);

  or or_1 (_3, _1, _2);
  or or_2 (_6, _4, _5);
  or or_3 (_8, _9, _10);
  or or_4 (_11, _12, _13);
endmodule

module IC_4073_3_Input_AND (
  input  in_1,
  input  in_2,
  input  in_3,
  input  in_4,
  input  in_5,
  input  in_6,
  input  in_7,
  input  in_8,
  input  in_9,
  input  in_10,
  input  in_11,
  output out_12,
  output out_13,
  output out_14
);

  and and_1 (out_12, in_2, in_3, in_4);
  and and_2 (out_13, in_5, in_6, in_7);
  and and_3 (out_14, in_8, in_9, in_10);
endmodule

module IC_4075_3_Input_OR (
  input  in_1,
  input  in_2,
  input  in_3,
  input  in_4,
  input  in_5,
  input  in_6,
  input  in_7,
  input  in_8,
  input  in_9,
  input  in_10,
  input  in_11,
  output out_12,
  output out_13,
  output out_14
);

  or or_1 (out_12, in_2, in_3, in_4);
  or or_2 (out_13, in_5, in_6, in_7);
  or or_3 (out_14, in_8, in_9, in_10);
endmodule

module IC_7486_XOR (
  input  in_1,
  input  in_2,
  input  in_3,
  input  in_4,
  input  in_5,
  input  in_6,
  input  in_7,
  input  in_8,
  input  in_9,
  input  in_10,
  output out_11,
  output out_12,
  output out_13,
  output out_14
);

  xor xor_1 (out_11, in_2, in_3);
  xor xor_2 (out_12, in_4, in_5);
  xor xor_3 (out_13, in_6, in_7);
  xor xor_4 (out_14, in_8, in_9);
endmodule

module _8_to_1_MUX (
  input  I0,
  input  I1,
  input  I2,
  input  I3,
  input  I4,
  input  I5,
  input  I6,
  input  I7,
  input  S0,
  input  S1,
  input  S2,
  output Y
);

  wire n4_1_mux_1_f, n4_1_mux_2_f;

  _4_1_MUX u_4_1_mux_1 (.F(n4_1_mux_1_f), .I3(I3), .I2(I2), .I1(I1), .I0(I0), .S1(S1), .S0(S0));
  _4_1_MUX u_4_1_mux_2 (.F(n4_1_mux_2_f), .I3(I7), .I2(I6), .I1(I5), .I0(I4), .S1(S1), .S0(S0));
  Multiplexer #(.enable("false")) multiplexer_1 (.in0(n4_1_mux_1_f), .in1(n4_1_mux_2_f), .out(Y), .sel(S2));
endmodule

module _4_1_MUX (
  input  I3,
  input  I2,
  input  I1,
  input  I0,
  input  S1,
  input  S0,
  output F
);

  wire and_1_out, and_2_out, and_3_out, and_4_out, not_1_out, not_2_out, or_1_out, or_2_out;

  not not_1 (not_1_out, S0);
  not not_2 (not_2_out, S1);
  and and_1 (and_1_out, I0, not_2_out, not_1_out);
  and and_2 (and_2_out, not_2_out, S0, I1);
  and and_3 (and_3_out, S1, not_1_out, I2);
  and and_4 (and_4_out, S0, S1, I3);
  or or_1 (or_1_out, and_1_out, and_2_out);
  or or_2 (or_2_out, and_3_out, and_4_out);
  or or_3 (F, or_1_out, or_2_out);
endmodule

module JK_FF (
  input  GND,
  input  VCC,
  input  in_3,
  input  in_4,
  input  CLK,
  input  in_6,
  input  in_7,
  input  CLK_2,
  input  CLR,
  input  PRESET,
  output out_11,
  output out_12,
  output out_13,
  output out_14
);

  J_K_Flip_Flop j_k_ff_1 (
    .J(in_3), .clk(CLK), .K(in_4), .Q(out_11), .Qn(out_12), .preset(CLR), .en(1'b1), .reset(PRESET));
  J_K_Flip_Flop j_k_ff_2 (
    .J(in_6), .clk(CLK_2), .K(in_7), .Q(out_13), .Qn(out_14), .preset(CLR), .en(1'b1), .reset(PRESET));
endmodule

module D_FF (
  input  in_1,
  input  in_2,
  input  in_3,
  input  in_4,
  output out_5,
  output out_6
);

  D_Flip_Flop d_ff_1 (.clk(in_1), .D(in_2), .Q(out_5), .Qn(out_6), .preset(in_4), .en(1'b1), .reset(in_3));
endmodule

module T_FF (
  input  in_1,
  input  in_2,
  input  in_3,
  input  in_4,
  output out_5,
  output out_6
);

  T_Flip_Flop t_ff_1 (.clk(in_1), .T(in_2), .Q(out_5), .Qn(out_6), .preset(in_3), .reset(in_4), .en(1'b1));
endmodule

module _7_segment_display (
  input  a,
  input  b,
  input  c,
  input  d,
  input  in_5,
  input  in_6,
  output out_7,
  output out_8,
  output out_9,
  output out_10,
  output out_11,
  output out_12,
  output out_13
);

  wire and_1_out, and_2_out, and_3_out, and_4_out, and_5_out, and_6_out, and_7_out, and_8_out, and_9_out,
       and_10_out, and_11_out, and_12_out, and_13_out, and_14_out, and_15_out, and_16_out, and_17_out,
       and_18_out, and_19_out, and_20_out, and_21_out, and_22_out, and_23_out, and_24_out, and_25_out,
       and_26_out, and_27_out, and_28_out, and_29_out, and_30_out, and_31_out, and_32_out, and_33_out,
       not_1_out, not_2_out, not_3_out, not_4_out, not_5_out, not_6_out, not_7_out, not_8_out, not_9_out,
       not_10_out, not_11_out, not_12_out, not_13_out, not_14_out, not_15_out, not_16_out, xor_1_out;

  not not_1 (not_1_out, a);
  not not_2 (not_2_out, d);
  not not_3 (not_3_out, c);
  not not_4 (not_4_out, b);
  not not_5 (not_5_out, d);
  not not_6 (not_6_out, a);
  not not_7 (not_7_out, b);
  not not_8 (not_8_out, d);
  not not_9 (not_9_out, c);
  not not_10 (not_10_out, a);
  not not_11 (not_11_out, b);
  not not_12 (not_12_out, a);
  not not_13 (not_13_out, d);
  not not_14 (not_14_out, b);
  not not_15 (not_15_out, d);
  not not_16 (not_16_out, c);
  and and_1 (and_1_out, c, not_12_out);
  and and_2 (and_2_out, a, not_13_out);
  and and_3 (and_3_out, b, c);
  and and_4 (and_4_out, c, not_13_out);
  and and_5 (and_5_out, not_12_out, b, d);
  and and_6 (and_6_out, not_14_out, not_15_out);
  and and_7 (and_7_out, a, not_14_out, not_16_out);
  and and_8 (and_8_out, not_14_out, not_12_out);
  and and_9 (and_9_out, not_12_out, c, d);
  and and_10 (and_10_out, d, not_16_out, a);
  and and_11 (and_11_out, not_1_out, not_16_out, not_2_out);
  xor xor_1 (xor_1_out, b, a);
  and and_12 (and_12_out, not_1_out, d);
  and and_13 (and_13_out, d, not_3_out);
  and and_14 (and_14_out, not_3_out, not_1_out);
  and and_15 (and_15_out, a, not_3_out);
  and and_16 (and_16_out, a, not_4_out, d);
  and and_17 (and_17_out, not_4_out, not_3_out, not_5_out);
  and and_18 (and_18_out, b, c, not_5_out);
  and and_19 (and_19_out, b, not_3_out, d);
  and and_20 (and_20_out, not_6_out, not_4_out, c);
  and and_21 (and_21_out, c, a);
  and and_22 (and_22_out, not_5_out, c);
  and and_23 (and_23_out, a, b);
  and and_24 (and_24_out, not_7_out, not_8_out);
  and and_25 (and_25_out, not_8_out, b);
  and and_26 (and_26_out, not_7_out, a);
  and and_27 (and_27_out, not_9_out, not_8_out);
  and and_28 (and_28_out, c, a);
  and and_29 (and_29_out, b, not_10_out, not_9_out);
  and and_30 (and_30_out, not_11_out, a);
  and and_31 (and_31_out, c, not_11_out);
  and and_32 (and_32_out, c, not_8_out);
  and and_33 (and_33_out, d, a);
  or or_1 (out_7, and_1_out, and_2_out, and_3_out, and_4_out, and_5_out, and_6_out, and_7_out);
  or or_2 (out_8, and_6_out, and_8_out, and_9_out, and_10_out, and_11_out);
  or or_3 (out_9, xor_1_out, and_12_out, and_13_out, and_14_out);
  or or_4 (out_10, and_15_out, and_16_out, and_17_out, and_18_out, and_19_out, and_20_out);
  or or_5 (out_11, and_21_out, and_22_out, and_23_out, and_24_out);
  or or_6 (out_12, and_25_out, and_26_out, and_27_out, and_28_out, and_29_out);
  or or_7 (out_13, and_30_out, and_31_out, and_32_out, and_33_out, and_29_out);
endmodule

module Question_1 (
  input  X,
  input  PRESET,
  output A,
  output B,
  output Y
);

  wire CLK_out, CLR_out, d_ff_1_out_6, d_ff_2_out_6, ic_4073_3_input_and_1_out_12,
       ic_4073_3_input_and_1_out_13, ic_4073_3_input_and_1_out_14, ic_4073_3_input_and_2_out_14,
       ic_4075_3_input_or_1_out_12, ic_4075_3_input_or_1_out_13, ic_7404_not_1__2, ic_7408_and_1__3,
       ic_7408_and_1__6, ic_7408_and_1__8, ic_7408_and_1__11;

  IC_7404_NOT ic_7404_not_1 (
    ._1(X), ._2(ic_7404_not_1__2));  // open: GND_7, _3, _5, _9, _11, _13, VCC_14, _4, _6, _8, _10, _12
  IC_7408_AND ic_7408_and_1 (
    ._1(X), ._2(d_ff_2_out_6), ._4(ic_7404_not_1__2), ._5(d_ff_2_out_6), ._9(A), ._10(X), ._12(d_ff_2_out_6),
    ._13(d_ff_1_out_6), ._3(ic_7408_and_1__3), ._6(ic_7408_and_1__6), ._8(ic_7408_and_1__8),
    ._11(ic_7408_and_1__11));  // open: VCC_14, GND_7
  IC_4073_3_Input_AND ic_4073_3_input_and_1 (
    .in_2(B), .in_3(B), .in_4(X), .in_5(A), .in_6(d_ff_2_out_6), .in_7(d_ff_2_out_6),
    .in_8(ic_7404_not_1__2), .in_9(d_ff_1_out_6), .in_10(B), .out_12(ic_4073_3_input_and_1_out_12),
    .out_13(ic_4073_3_input_and_1_out_13), .out_14(ic_4073_3_input_and_1_out_14));  // open: in_1, in_11
  IC_4073_3_Input_AND ic_4073_3_input_and_2 (
    .in_8(X), .in_9(B), .in_10(d_ff_1_out_6), .out_14(ic_4073_3_input_and_2_out_14));  // open: in_1, in_2, in_3, in_4, in_5, in_6, in_7, in_11, out_12, out_13
  Clock CLK (.out(CLK_out));
  Button CLR (.out(CLR_out));
  IC_4075_3_Input_OR ic_4075_3_input_or_1 (
    .in_2(ic_7408_and_1__11), .in_3(ic_4073_3_input_and_1_out_14), .in_4(ic_7408_and_1__3),
    .in_5(ic_4073_3_input_and_1_out_12), .in_6(ic_7408_and_1__8), .in_7(ic_7408_and_1__6),
    .in_8(ic_7408_and_1__6), .in_9(ic_4073_3_input_and_1_out_13), .in_10(ic_4073_3_input_and_2_out_14),
    .out_12(ic_4075_3_input_or_1_out_12), .out_13(ic_4075_3_input_or_1_out_13), .out_14(Y));  // open: in_1, in_11
  D_FF d_ff_1 (
    .in_1(CLK_out), .in_2(ic_4075_3_input_or_1_out_13), .out_5(A), .out_6(d_ff_1_out_6), .in_3(PRESET),
    .in_4(CLR_out));
  D_FF d_ff_2 (
    .in_1(CLK_out), .in_2(ic_4075_3_input_or_1_out_12), .out_5(B), .out_6(d_ff_2_out_6), .in_3(PRESET),
    .in_4(CLR_out));

  // Notes on the sheet:
  //   B'
  //   B'X
  //   X'
  //   B'X'
  //   AB'
  //   A'
  //   A'B'
  //   A'BX'
  //   BX
  //   AX
  //   A'BX
  //   B'X'+AX+BX
  //   A'BX'+B'X+A'B'
  //   B'X'+AB'+A'BX
endmodule

module Question_2 (
  input  CLR,
  output Q1,
  output Q2,
  output Q3,
  output Q4,
  output Q5
);

  wire CLK_out;

  Clock CLK (.out(CLK_out));
  T_FF t_ff_1 (.in_1(CLK_out), .in_3(CLR), .out_6(Q1));  // open: in_2, in_4, out_5
  T_FF t_ff_2 (.in_1(CLK_out), .in_2(Q1), .in_3(CLR), .out_6(Q2));  // open: in_4, out_5
  T_FF t_ff_3 (.in_1(CLK_out), .in_2(Q2), .in_3(CLR), .out_6(Q3));  // open: in_4, out_5
  T_FF t_ff_4 (.in_1(CLK_out), .in_2(Q3), .in_3(CLR), .out_6(Q4));  // open: in_4, out_5
  T_FF t_ff_5 (.in_1(CLK_out), .in_2(Q4), .in_3(CLR), .out_6(Q5));  // open: in_4, out_5
endmodule

module Bonus_Q (
  input  J,
  input  PR,
  input  K,
  output Q,
  output Q_prime
);

  wire and_1_out, and_2_out, and_3_out, and_4_out, CLK_out, CLR_out, nor_1_out, nor_2_out, not_1_out,
       or_1_out, or_2_out;

  or or_1 (or_1_out, J, PR);
  or or_2 (or_2_out, PR, K);
  Clock CLK (.out(CLK_out));
  not not_1 (not_1_out, CLK_out);
  and and_1 (and_1_out, or_1_out, Q_prime, CLK_out);
  and and_2 (and_2_out, CLK_out, Q, or_2_out);
  Button CLR (.out(CLR_out));
  nor nor_1 (nor_1_out, and_1_out, nor_2_out);
  nor nor_2 (nor_2_out, and_2_out, nor_1_out, CLR_out);
  and and_3 (and_3_out, nor_1_out, not_1_out);
  and and_4 (and_4_out, nor_2_out, not_1_out);
  nor nor_3 (Q, and_3_out, Q_prime);
  nor nor_4 (Q_prime, and_4_out, Q);
endmodule
