// Logisim project Nawal Ayesha_1911301042 Lab 1.circ as structural Verilog: 8 circuits, main circuit main
module main (
  input  A,
  input  B,
  input  C,
  output F
);

  wire ic_7404_1__2, ic_7404_1__6, ic_7408_1__3, ic_7408_1__6, ic_7408_1__11, ic_7432_1__11;

  IC_7404 ic_7404_1 (
    ._1(A), ._5(B), ._2(ic_7404_1__2), ._6(ic_7404_1__6));  // open: GND_7, _3, _9, _11, _13, VCC_14, _4, _8, _10, _12
  IC_7408 ic_7408_1 (
    ._1(ic_7404_1__2), ._2(C), ._4(ic_7404_1__6), ._5(A), ._12(B), ._13(C), ._3(ic_7408_1__3),
    ._6(ic_7408_1__6), ._11(ic_7408_1__11));  // open: VCC_14, _9, _10, GND_7, _8
  IC_7432 ic_7432_1 (
    ._9(ic_7408_1__11), ._10(ic_7432_1__11), ._12(ic_7408_1__6), ._13(ic_7408_1__3), ._8(F),
    ._11(ic_7432_1__11));  // open: VCC_14, _1, _2, _4, _5, GND_7, _3, _6

  // Notes on the sheet:
  //   B'
  //   A'
  //   A'C
  //   AB'
  //   BC
endmodule

module IC_7404 (
  input  GND_7,
  input  _1,
  input  _3,
  input  _5,
  input  _9,
  input  _11,
  input  _13,
  input  VCC_14,
  output _2,
  output _4,
  output _6,
  output _8,
  output _10,
  output _12
);

  not not_1 (_2, _1);
  not not_2 (_4, _3);
  not not_3 (_6, _5);
  not not_4 (_8, _9);
  not not_5 (_10, _11);
  not not_6 (_12, _13);
endmodule

module IC_7408 (
  input  VCC_14,
  input  _1,
  input  _2,
  input  _4,
  input  _5,
  input  _9,
  input  _10,
  input  _12,
  input  _13,
  input  GND_7,
  output _3,
  output _6,
  output _8,
  output _11
);

  and and_1 (_3, _1, _2);
  and and_2 (_6, _4, _5);
  and and_3 (_8, _9, _10);
  and and_4 (_11, _12, _13);
endmodule

module IC_7432 (
  input  VCC_14,
  input  _1,
  input  _2,
  input  _4,
  input  _5,
  input  _9,
  input  _10,
  input  _12,
  input  _13,
  input  GND_7,
  output _3,
  output _6,
  output _8,
  output _11
);

  or or_1 (_3, _1, _2);
  or or_2 (_6, _4, _5);
  or or_3 (_8, _9, _10);
  or or_4 (_11, _12, _13);
endmodule

module IC_7400 (
  input  VCC_14,
  input  _1,
  input  _2,
  input  _4,
  input  _5,
  input  _9,
  input  _10,
  input  _12,
  input  _13,
  input  GND_7,
  output _3,
  output _6,
  output _8,
  output _11
);

  nand nand_1 (_3, _1, _2);
  nand nand_2 (_6, _4, _5);
  nand nand_3 (_8, _9, _10);
  nand nand_4 (_11, _12, _13);
endmodule

module Exp_1 (
  input  in_1,
  input  in_2,
  output out_3,
  output out_4,
  output out_5,
  output out_6,
  output out_7
);

  IC_7404 ic_7404_1 (
    ._1(in_2), ._3(in_1), ._2(out_3), ._4(out_5));  // open: GND_7, _5, _9, _11, _13, VCC_14, _6, _8, _10, _12
  IC_7432 ic_7432_1 (._1(in_2), ._2(in_1), ._3(out_7));  // open: VCC_14, _4, _5, _9, _10, _12, _13, GND_7, _6, _8, _11
  IC_7408 ic_7408_1 (._1(in_2), ._2(in_1), ._3(out_4));  // open: VCC_14, _4, _5, _9, _10, _12, _13, GND_7, _6, _8, _11
  IC_7400 ic_7400_1 (._1(in_1), ._2(in_2), ._3(out_6));  // open: VCC_14, _4, _5, _9, _10, _12, _13, GND_7, _6, _8, _11
endmodule

module Exp_2 (
  input  A,
  input  B,
  input  C,
  input  A_2,
  input  B_2,
  input  C_2,
  output F,
  output F_2
);

  wire and_1_out, or_1_out;

  and and_1 (and_1_out, A, B);
  and and_2 (F, and_1_out, C);
  or or_1 (or_1_out, A_2, B_2);
  or or_2 (F_2, or_1_out, C_2);
endmodule

module Exp_3_1 (
  input  A,
  input  B,
  input  C,
  output I1,
  output F,
  output I2,
  output I3
);

  wire not_1_out, not_2_out;

  not not_1 (not_1_out, A);
  not not_2 (not_2_out, B);
  and A_prime_C (I1, C, not_1_out);
  and AB_prime (I2, A, not_2_out);
  and BC (I3, B, C);
  or or_1 (F, I1, I2, I3);
endmodule
