// Logisim project Nawal Ayesha_1911301042 Lab 2.circ as structural Verilog: 7 circuits, main circuit main
module main (
  input  A,
  input  B,
  input  C,
  output F
);

  wire and_1_out, and_2_out, not_1_out;

  not not_1 (not_1_out, C);
  and and_1 (and_1_out, A, C);
  and and_2 (and_2_out, B, not_1_out);
  or or_1 (F, and_1_out, and_2_out);
endmodule

module IC_7400 (
  input  VCC_14,
  input  _1,
  input  _2,
  input  _4,
  input  _5,
  input  _9,
  input  _10,
  input  _12,
  input  _13,
  input  GND_7,
  output _3,
  output _6,
  output _8,
  output _11
);

  nand nand_1 (_3, _1, _2);
  nand nand_2 (_6, _4, _5);
  nand nand_3 (_8, _9, _10);
  nand nand_4 (_11, _12, _13);
endmodule

module NAND_implementation (
  input  A,
  input  in_2,
  input  A_2,
  input  in_4,
  input  B,
  input  in_6,
  input  A_3,
  input  in_8,
  input  in_9,
  input  B_2,
  output out_11,
  output out_12,
  output A_B,
  output out_14,
  output A_B_2,
  output out_16
);

  wire A_A__prime_2_out, A_B__prime_out, B_B__prime_out;

  nand A_A__prime (out_11, A, A);
  nand A_B__prime (A_B__prime_out, A_2, B);
  nand A_A__prime_2 (A_A__prime_2_out, A_3, A_3);
  nand B_B__prime (B_B__prime_out, B_2, B_2);
  nand A_prime_B_prime__prime (A_B, A_B__prime_out, A_B__prime_out);
  nand A_prime_B_prime__prime_2 (A_B_2, A_A__prime_2_out, B_B__prime_out);
  not not_1 (out_12, in_2);
  and and_1 (out_14, in_4, in_6);
  or or_1 (out_16, in_8, in_9);
endmodule

module Exp_F2_NOR (
  input  A,
  input  in_2,
  input  A_2,
  input  in_4,
  input  in_5,
  input  B,
  input  A_3,
  input  in_8,
  input  B_2,
  input  in_10,
  input  A_4,
  input  in_12,
  input  in_13,
  input  B_3,
  input  A_5,
  input  in_16,
  input  in_17,
  input  B_4,
  output out_19,
  output out_20,
  output A_B,
  output out_22,
  output A_B_2,
  output out_24,
  output out_25,
  output out_26,
  output out_27,
  output out_28
);

  wire A_A__prime_2_out, A_B__prime_out, B_B__prime_out, nor_1_out, nor_2_out, nor_3_out, nor_4_out,
       nor_5_out, nor_6_out, nor_8_out;

  nor A_A__prime (out_19, A, A);
  nor A_A__prime_2 (A_A__prime_2_out, A_2, A_2);
  nor B_B__prime (B_B__prime_out, B, B);
  nor A_B__prime (A_B__prime_out, A_3, B_2);
  nor nor_1 (nor_1_out, A_4, B_3);
  nor nor_2 (nor_2_out, A_5, B_4);
  nor A_prime_B_prime__prime (A_B_2, A_B__prime_out, A_B__prime_out);
  nor nor_3 (nor_3_out, A_4, nor_1_out);
  nor nor_4 (nor_4_out, nor_1_out, B_3);
  nor nor_5 (nor_5_out, A_5, nor_2_out);
  nor nor_6 (nor_6_out, nor_2_out, B_4);
  nor A_prime_B_prime__prime_2 (A_B, A_A__prime_2_out, B_B__prime_out);
  nor nor_7 (out_25, nor_3_out, nor_4_out);
  nor nor_8 (nor_8_out, nor_5_out, nor_6_out);
  nor nor_9 (out_27, nor_8_out, nor_8_out);
  not not_1 (out_20, in_2);
  and and_1 (out_22, in_4, in_5);
  or or_1 (out_24, in_8, in_10);
  xnor xnor_1 (out_26, in_12, in_13);
  xor xor_1 (out_28, in_16, in_17);
endmodule

module Exp_F1_NAND (
  input  A,
  input  in_2,
  input  in_3,
  input  B,
  input  A_2,
  input  in_6,
  input  in_7,
  input  B_2,
  output out_9,
  output out_10,
  output out_11,
  output out_12
);

  wire nand_1_out, nand_2_out, nand_3_out, nand_4_out, nand_5_out, nand_6_out, nand_8_out;

  nand nand_1 (nand_1_out, A, B);
  nand nand_2 (nand_2_out, A_2, B_2);
  nand nand_3 (nand_3_out, A, nand_1_out);
  nand nand_4 (nand_4_out, nand_1_out, B);
  nand nand_5 (nand_5_out, A_2, nand_2_out);
  nand nand_6 (nand_6_out, nand_2_out, B_2);
  nand nand_7 (out_9, nand_3_out, nand_4_out);
  nand nand_8 (nand_8_out, nand_5_out, nand_6_out);
  nand nand_9 (out_12, nand_8_out, nand_8_out);
  xor xor_1 (out_10, in_2, in_3);
  xnor xnor_1 (out_11, in_6, in_7);
endmodule

module Exp_D2_using_NAND (
  input  A,
  input  B,
  input  C,
  output F,
  output Y
);

  wire nand_1_out, nand_2_out, nand_3_out, nand_4_out, nand_5_out, nand_6_out, nand_7_out, nand_8_out,
       nand_9_out, nand_10_out;

  nand nand_1 (nand_1_out, C, C);
  nand nand_2 (nand_2_out, C, C);
  nand nand_3 (nand_3_out, A, C);
  nand nand_4 (nand_4_out, nand_1_out, B);
  nand nand_5 (nand_5_out, A, C);
  nand nand_6 (nand_6_out, nand_2_out, B);
  nand nand_7 (nand_7_out, nand_3_out, nand_3_out);
  nand nand_8 (nand_8_out, nand_4_out, nand_4_out);
  nand nand_9 (nand_9_out, nand_7_out, nand_7_out);
  nand nand_10 (nand_10_out, nand_8_out, nand_8_out);
  nand nand_11 (F, nand_9_out, nand_10_out);
  nand nand_12 (Y, nand_5_out, nand_6_out);

  // Notes on the sheet:
  //   C'
  //   C'
  //   Simplified Circuit
  //   BC'
  //   AC
  //   BC'
  //   AC
  //   AC+BC'
  //   AC+BC'
endmodule

module Exp_D2_using_NOR (
  input  A,
  input  B,
  input  C,
  output F
);

  wire nor_1_out, nor_2_out, nor_3_out, nor_4_out, nor_5_out, nor_6_out, nor_7_out, nor_8_out;

  nor nor_1 (nor_1_out, C, C);
  nor nor_2 (nor_2_out, C, C);
  nor nor_3 (nor_3_out, A, A);
  nor nor_4 (nor_4_out, nor_1_out, nor_1_out);
  nor nor_5 (nor_5_out, B, B);
  nor nor_6 (nor_6_out, nor_3_out, nor_2_out);
  nor nor_7 (nor_7_out, nor_4_out, nor_5_out);
  nor nor_8 (nor_8_out, nor_6_out, nor_7_out);
  nor AC_BC_prime (F, nor_8_out, nor_8_out);

  // Notes on the sheet:
  //   C'
  //   AC
  //   BC'
endmodule
