// Logisim project Nawal Ayesha_1911301042 Lab 3.circ as structural Verilog: 6 circuits, main circuit main
module main (
  input  A,
  input  B,
  input  C,
  output F
);

  wire ic_4073_and_1_out_12, ic_4075_or_1_out_12, ic_4075_or_1_out_13, ic_4075_or_1_out_14,
       ic_4075_or_2_out_12, ic_4075_or_2_out_13, ic_7404_not_1_out_9, ic_7404_not_1_out_10,
       ic_7404_not_1_out_14;

  IC_7404_NOT ic_7404_not_1 (
    .in_2(C), .in_3(B), .in_7(A), .out_9(ic_7404_not_1_out_9), .out_10(ic_7404_not_1_out_10),
    .out_14(ic_7404_not_1_out_14));  // open: in_1, in_4, in_5, in_6, in_8, out_11, out_12, out_13
  IC_4075_OR ic_4075_or_1 (
    .in_2(A), .in_3(B), .in_4(C), .in_5(A), .in_6(ic_7404_not_1_out_10), .in_7(ic_7404_not_1_out_9),
    .in_8(C), .in_9(B), .in_10(ic_7404_not_1_out_14), .out_12(ic_4075_or_1_out_12),
    .out_13(ic_4075_or_1_out_13), .out_14(ic_4075_or_1_out_14));  // open: in_1, in_11
  IC_4075_OR ic_4075_or_2 (
    .in_2(B), .in_3(ic_7404_not_1_out_9), .in_4(ic_7404_not_1_out_14), .in_5(ic_7404_not_1_out_10),
    .in_6(ic_7404_not_1_out_9), .in_7(ic_7404_not_1_out_14), .out_12(ic_4075_or_2_out_12),
    .out_13(ic_4075_or_2_out_13));  // open: in_1, in_8, in_9, in_10, in_11, out_14
  IC_4073_AND ic_4073_and_1 (
    .in_2(ic_4075_or_1_out_14), .in_3(ic_4075_or_1_out_12), .in_4(ic_4075_or_1_out_13),
    .in_8(ic_4073_and_1_out_12), .in_9(ic_4075_or_2_out_12), .in_10(ic_4075_or_2_out_13),
    .out_12(ic_4073_and_1_out_12), .out_14(F));  // open: in_1, in_5, in_6, in_7, in_11, out_13

  // Notes on the sheet:
  //   C'
  //   B'
  //   (A+B'+C')
  //   (A'+B'+C')
  //   Maxterm IC circuit 
  //   A'
  //   (A'+B+C')
  //   (A'+B+C)
  //   (A+B+C)
endmodule

module IC_7404_NOT (
  input  in_1,
  input  in_2,
  input  in_3,
  input  in_4,
  input  in_5,
  input  in_6,
  input  in_7,
  input  in_8,
  output out_9,
  output out_10,
  output out_11,
  output out_12,
  output out_13,
  output out_14
);

  not not_1 (out_9, in_2);
  not not_2 (out_10, in_3);
  not not_3 (out_11, in_4);
  not not_4 (out_12, in_5);
  not not_5 (out_13, in_6);
  not not_6 (out_14, in_7);
endmodule

module IC_4073_AND (
  input  in_1,
  input  in_2,
  input  in_3,
  input  in_4,
  input  in_5,
  input  in_6,
  input  in_7,
  input  in_8,
  input  in_9,
  input  in_10,
  input  in_11,
  output out_12,
  output out_13,
  output out_14
);

  and and_1 (out_12, in_2, in_3, in_4);
  and and_2 (out_13, in_5, in_6, in_7);
  and and_3 (out_14, in_8, in_9, in_10);
endmodule

module IC_4075_OR (
  input  in_1,
  input  in_2,
  input  in_3,
  input  in_4,
  input  in_5,
  input  in_6,
  input  in_7,
  input  in_8,
  input  in_9,
  input  in_10,
  input  in_11,
  output out_12,
  output out_13,
  output out_14
);

  or or_1 (out_12, in_2, in_3, in_4);
  or or_2 (out_13, in_5, in_6, in_7);
  or or_3 (out_14, in_8, in_9, in_10);
endmodule

module Minterm_Circuit (
  input  A,
  input  B,
  input  C,
  output F
);

  wire ic_4073_and_1_out_12, ic_4073_and_1_out_13, ic_4073_and_1_out_14, ic_7404_not_1_out_9,
       ic_7404_not_1_out_10, ic_7404_not_1_out_11;

  IC_7404_NOT ic_7404_not_1 (
    .in_2(A), .in_3(B), .in_4(C), .out_9(ic_7404_not_1_out_9), .out_10(ic_7404_not_1_out_10),
    .out_11(ic_7404_not_1_out_11));  // open: in_1, in_5, in_6, in_7, in_8, out_12, out_13, out_14
  IC_4073_AND ic_4073_and_1 (
    .in_2(B), .in_3(A), .in_4(ic_7404_not_1_out_11), .in_5(ic_7404_not_1_out_9), .in_6(ic_7404_not_1_out_10),
    .in_7(C), .in_8(ic_7404_not_1_out_11), .in_9(B), .in_10(ic_7404_not_1_out_9),
    .out_12(ic_4073_and_1_out_12), .out_13(ic_4073_and_1_out_13), .out_14(ic_4073_and_1_out_14));  // open: in_1, in_11
  IC_4075_OR ic_4075_or_1 (
    .in_5(ic_4073_and_1_out_13), .in_6(ic_4073_and_1_out_14), .in_7(ic_4073_and_1_out_12), .out_13(F));  // open: in_1, in_2, in_3, in_4, in_8, in_9, in_10, in_11, out_12, out_14

  // Notes on the sheet:
  //   A'
  //   B'
  //   C'
  //   A'B'C
  //   A'BC'
  //   ABC'
  //   ABC'+A'BC'+A'B'C
endmodule

module Maxterm_circuit (
  input  A,
  input  B,
  input  C,
  output F
);

  wire and_1_out, not_1_out, not_2_out, not_3_out, or_1_out, or_2_out, or_3_out, or_4_out, or_5_out;

  not not_1 (not_1_out, A);
  not not_2 (not_2_out, B);
  not not_3 (not_3_out, C);
  or or_1 (or_1_out, C, B, A);
  or or_2 (or_2_out, not_3_out, not_2_out, A);
  or or_3 (or_3_out, B, C, not_1_out);
  or or_4 (or_4_out, not_3_out, B, not_1_out);
  or or_5 (or_5_out, not_3_out, not_2_out, not_1_out);
  and and_1 (and_1_out, or_1_out, or_2_out, or_3_out);
  and and_2 (F, and_1_out, or_4_out, or_5_out);

  // Notes on the sheet:
  //   A'
  //   B'
  //   C'
  //   A+B+C
  //   A+B'+C'
  //   A'+B+C
  //   A'+B+C'
  //   A'+B'+C'
  //   (A+B+C)(A+B'+C')(A'+B+C)
  //   (A+B+C)(A+B'+C')(A'+B+C)(A'+B+C')(A'+B'+C')
endmodule
