// Logisim project Nawal Ayesha_1911301042 Lab 4.circ as structural Verilog
module IC_7404_NOT (
  input  in_1,
  input  in_2,
  input  in_3,
  input  in_4,
  input  in_5,
  input  in_6,
  input  in_7,
  input  in_8,
  output out_9,
  output out_10,
  output out_11,
  output out_12,
  output out_13,
  output out_14
);

  not not_1 (out_9, in_2);
  not not_2 (out_10, in_3);
  not not_3 (out_11, in_4);
  not not_4 (out_12, in_5);
  not not_5 (out_13, in_6);
  not not_6 (out_14, in_7);
endmodule

module IC_4073_AND (
  input  in_1,
  input  in_2,
  input  in_3,
  input  in_4,
  input  in_5,
  input  in_6,
  input  in_7,
  input  in_8,
  input  in_9,
  input  in_10,
  input  in_11,
  output out_12,
  output out_13,
  output out_14
);

  and and_1 (out_12, in_2, in_3, in_4);
  and and_2 (out_13, in_5, in_6, in_7);
  and and_3 (out_14, in_8, in_9, in_10);
endmodule

module IC_4075_OR (
  input  in_1,
  input  in_2,
  input  in_3,
  input  in_4,
  input  in_5,
  input  in_6,
  input  in_7,
  input  in_8,
  input  in_9,
  input  in_10,
  input  in_11,
  output out_12,
  output out_13,
  output out_14
);

  or or_1 (out_12, in_2, in_3, in_4);
  or or_2 (out_13, in_5, in_6, in_7);
  or or_3 (out_14, in_8, in_9, in_10);
endmodule

module IC_7400_NAND (
  input  in_1,
  input  in_2,
  input  in_3,
  input  in_4,
  input  in_5,
  input  in_6,
  input  in_7,
  input  in_8,
  input  in_9,
  input  in_10,
  output out_11,
  output out_12,
  output out_13,
  output out_14
);

  nand nand_1 (out_11, in_2, in_3);
  nand nand_2 (out_12, in_4, in_5);
  nand nand_3 (out_13, in_6, in_7);
  nand nand_4 (out_14, in_8, in_9);
endmodule

module IC_7408_AND (
  input  in_1,
  input  in_2,
  input  in_3,
  input  in_4,
  input  in_5,
  input  in_6,
  input  in_7,
  input  in_8,
  input  in_9,
  input  in_10,
  output out_11,
  output out_12,
  output out_13,
  output out_14
);

  and and_1 (out_11, in_2, in_3);
  and and_2 (out_12, in_4, in_5);
  and and_3 (out_13, in_6, in_7);
  and and_4 (out_14, in_8, in_9);
endmodule

module BCD_to_EXCESS_3_Basic_gates (
  input  W,
  input  X,
  input  Y,
  input  Z,
  output A,
  output B,
  output C,
  output D
);

  wire and_1_out, and_2_out, and_3_out, and_4_out, and_5_out, and_6_out, and_7_out, not_1_out, not_2_out;

  not not_1 (not_1_out, Y);
  not not_2 (not_2_out, X);
  not not_3 (D, Z);
  and and_1 (and_1_out, Z, X);
  and and_2 (and_2_out, Y, X);
  and and_3 (and_3_out, not_2_out, Z);
  and and_4 (and_4_out, not_2_out, Y);
  and and_5 (and_5_out, Y, Z);
  and and_6 (and_6_out, D, not_1_out);
  and and_7 (and_7_out, X, D, not_1_out);
  or or_1 (A, and_1_out, and_2_out, W);
  or or_2 (C, and_5_out, and_6_out);
  or or_3 (B, and_3_out, and_4_out, and_7_out);

  // Notes on the sheet:
  //   XZ
  //   XY
  //   W
  //   X'Z
  //   X'Y
  //   YZ
  //   Y'Z'
  //   XY'Z'
  //   Z'
  //   YZ+Y'Z'
  //   XZ+XY+W
  //   X'Y+X'Z+XY'Z'
endmodule

module BCD_to_EXCESS_3_IC (
  input  W,
  input  X,
  input  Y,
  input  Z,
  output A,
  output B,
  output C,
  output D
);

  wire ic_4073_and_1_out_13, ic_7404_not_1_out_9, ic_7404_not_1_out_12, ic_7408_and_1_out_11,
       ic_7408_and_1_out_12, ic_7408_and_1_out_13, ic_7408_and_1_out_14, ic_7408_and_2_out_11,
       ic_7408_and_2_out_14;

  IC_4075_OR ic_4075_or_1 (
    .in_2(ic_7408_and_2_out_11), .in_3(ic_7408_and_2_out_14), .in_4(ic_7408_and_2_out_11),
    .in_5(ic_7408_and_1_out_12), .in_6(ic_7408_and_1_out_11), .in_7(W), .in_8(ic_7408_and_1_out_14),
    .in_9(ic_4073_and_1_out_13), .in_10(ic_7408_and_1_out_13), .out_12(C), .out_13(A), .out_14(B));  // open: in_1, in_11
  IC_7408_AND ic_7408_and_1 (
    .in_2(Y), .in_3(X), .in_4(Z), .in_5(X), .in_6(ic_7404_not_1_out_9), .in_7(Y), .in_8(ic_7404_not_1_out_9),
    .in_9(Z), .out_11(ic_7408_and_1_out_11), .out_12(ic_7408_and_1_out_12), .out_13(ic_7408_and_1_out_13),
    .out_14(ic_7408_and_1_out_14));  // open: in_1, in_10
  IC_7404_NOT ic_7404_not_1 (
    .in_2(X), .in_5(Y), .in_7(Z), .out_9(ic_7404_not_1_out_9), .out_12(ic_7404_not_1_out_12), .out_14(D));  // open: in_1, in_3, in_4, in_6, in_8, out_10, out_11, out_13
  IC_4073_AND ic_4073_and_1 (
    .in_5(D), .in_6(ic_7404_not_1_out_12), .in_7(X), .out_13(ic_4073_and_1_out_13));  // open: in_1, in_2, in_3, in_4, in_8, in_9, in_10, in_11, out_12, out_14
  IC_7408_AND ic_7408_and_2 (
    .in_2(ic_7404_not_1_out_12), .in_3(D), .in_8(Y), .in_9(Z), .out_11(ic_7408_and_2_out_11),
    .out_14(ic_7408_and_2_out_14));  // open: in_1, in_4, in_5, in_6, in_7, in_10, out_12, out_13

  // Notes on the sheet:
  //   XY
  //   XZ
  //   XY+XZ+W
  //   X'Z
  //   X'Y
  //   x'z+x'y+xy'z'
  //   YZ+Y'Z'
  //   X'
  //   Z'
  //   Z'
  //   Y'
  //   XY'Z'
  //   Y'Z'
  //   YZ
endmodule

module BCD_to_EXCESS_3_Universal_gates (
  input  W,
  input  X,
  input  Y,
  input  Z,
  output A,
  output B,
  output C,
  output D
);

  wire nand_1_out, nand_2_out, nand_4_out, nand_5_out, nand_6_out, nand_7_out, nand_8_out, nand_9_out,
       nand_10_out, nand_11_out, nand_12_out, nand_13_out, nand_15_out;

  nand nand_1 (nand_1_out, Y, Y);
  nand nand_2 (nand_2_out, X, X);
  nand nand_3 (D, Z, Z);
  nand nand_4 (nand_4_out, Z, X);
  nand nand_5 (nand_5_out, Y, X);
  nand nand_6 (nand_6_out, W, W);
  nand nand_7 (nand_7_out, Y, nand_2_out);
  nand nand_8 (nand_8_out, nand_2_out, Z);
  nand nand_9 (nand_9_out, Z, Z);
  nand nand_10 (nand_10_out, Y, Y);
  nand nand_11 (nand_11_out, Z, Z);
  nand nand_12 (nand_12_out, Z, Y);
  nand nand_13 (nand_13_out, nand_11_out, nand_1_out);
  nand nand_14 (A, nand_4_out, nand_5_out, nand_6_out);
  nand nand_15 (nand_15_out, nand_9_out, nand_10_out, X);
  nand nand_16 (C, nand_12_out, nand_13_out);
  nand nand_17 (B, nand_7_out, nand_8_out, nand_15_out);

  // Notes on the sheet:
  //   Y'
  //   X'
  //   (XZ)'
  //   (XY)'
  //   W'
  //   (X'Y)'
  //   (X'Z)'
  //   Z'
  //   Y'
  //   Z'
  //   (YZ)'
  //   (Y'Z')'
  //   W+XY+XZ
  //   (XY'Z')'
  //   YZ+Y'Z'
  //   Z'
  //   X'Y+X'Z+XY'Z'
endmodule
