// Logisim project Nawal Ayesha_1911301042 Lab 5.circ as structural Verilog
module IC_7408_AND (
  input  VCC_14,
  input  _1,
  input  _2,
  input  _4,
  input  _5,
  input  _9,
  input  _10,
  input  _12,
  input  _13,
  input  GND_7,
  output _3,
  output _6,
  output _8,
  output _11
);

  and and_1 (_3, _1, _2);
  and and_2 (_6, _4, _5);
  and and_3 (_8, _9, _10);
  and and_4 (_11, _12, _13);
endmodule

module IC_7432_OR (
  input  VCC_14,
  input  _1,
  input  _2,
  input  _4,
  input  _5,
  input  _9,
  input  _10,
  input  _12,
  input  _13,
  input  GND_7,
  output _3,
  output _6,
  output _8,
  output _11
);

  or or_1 (_3, _1, _2);
  or or_2 (_6, _4, _5);
  or or_3 (_8, _9, _10);
  or or_4 (_11, _12, _13);
endmodule

module IC_7486_XOR (
  input  in_1,
  input  in_2,
  input  in_3,
  input  in_4,
  input  in_5,
  input  in_6,
  input  in_7,
  input  in_8,
  input  in_9,
  input  in_10,
  output out_11,
  output out_12,
  output out_13,
  output out_14
);

  xor xor_1 (out_11, in_2, in_3);
  xor xor_2 (out_12, in_4, in_5);
  xor xor_3 (out_13, in_6, in_7);
  xor xor_4 (out_14, in_8, in_9);
endmodule

module IC_7483 (
  input  VCC,
  input  GND,
  input  A4,
  input  A3,
  input  A2,
  input  A1,
  input  C,
  input  B1,
  input  B4,
  input  B3,
  input  B2,
  output Carry_Out,
  output S4,
  output S3,
  output S2,
  output S1
);

  wire and_1_out, and_2_out, and_3_out, and_4_out, and_5_out, and_6_out, and_7_out, and_8_out, or_2_out,
       or_3_out, or_4_out, xor_1_out, xor_2_out, xor_3_out, xor_4_out;

  xor xor_1 (xor_1_out, A1, B1);
  and and_1 (and_1_out, A1, B1);
  xor xor_2 (xor_2_out, A4, B4);
  and and_2 (and_2_out, A4, B4);
  xor xor_3 (xor_3_out, A2, B2);
  and and_3 (and_3_out, A2, B2);
  xor xor_4 (xor_4_out, A3, B3);
  and and_4 (and_4_out, A3, B3);
  xor xor_5 (S1, xor_1_out, C);
  and and_5 (and_5_out, xor_1_out, C);
  xor xor_6 (S4, xor_2_out, or_4_out);
  and and_6 (and_6_out, xor_2_out, or_4_out);
  xor xor_7 (S2, xor_3_out, or_2_out);
  and and_7 (and_7_out, xor_3_out, or_2_out);
  xor xor_8 (S3, xor_4_out, or_3_out);
  and and_8 (and_8_out, xor_4_out, or_3_out);
  or or_1 (Carry_Out, and_6_out, and_2_out);
  or or_2 (or_2_out, and_5_out, and_1_out);
  or or_3 (or_3_out, and_7_out, and_3_out);
  or or_4 (or_4_out, and_8_out, and_4_out);

  // Notes on the sheet:
  //   C1
  //   C2
endmodule

module Experiment_1 (
  input  A4,
  input  A3,
  input  A2,
  input  A1,
  input  B4,
  input  B3,
  input  B2,
  input  B1,
  input  M,
  output Carry_Out,
  output S4,
  output S3,
  output S2,
  output S1
);

  wire ic_7486_xor_1_out_11, ic_7486_xor_1_out_12, ic_7486_xor_1_out_13, ic_7486_xor_1_out_14;

  IC_7486_XOR ic_7486_xor_1 (
    .in_2(B1), .in_3(M), .in_4(B2), .in_5(M), .in_6(M), .in_7(B4), .in_8(B3), .in_9(M),
    .out_11(ic_7486_xor_1_out_11), .out_12(ic_7486_xor_1_out_12), .out_13(ic_7486_xor_1_out_13),
    .out_14(ic_7486_xor_1_out_14));  // open: in_1, in_10
  IC_7483 ic_7483_1 (
    .B1(ic_7486_xor_1_out_11), .B4(ic_7486_xor_1_out_13), .B3(ic_7486_xor_1_out_14),
    .B2(ic_7486_xor_1_out_12), .A4(A4), .A3(A3), .A2(A2), .A1(A1), .C(M), .Carry_Out(Carry_Out), .S4(S4),
    .S3(S3), .S2(S2), .S1(S1));  // open: VCC, GND
endmodule

module Experiment_3 (
  input  A4,
  input  A3,
  input  A2,
  input  A1,
  input  B4,
  input  B3,
  input  B2,
  input  B1,
  input  Carry_In,
  input  in_10,
  output Carry,
  output S4,
  output S3,
  output S2,
  output S1
);

  wire ic_7408_and_1__3, ic_7408_and_1__6, ic_7432_or_1__11, ic_7483_1_carry_out, ic_7483_1_s1, ic_7483_1_s2,
       ic_7483_1_s3, ic_7483_1_s4;

  IC_7483 ic_7483_1 (
    .B1(B1), .B4(B4), .B3(B3), .B2(B2), .A4(A4), .A3(A3), .A2(A2), .A1(A1), .C(Carry_In),
    .Carry_Out(ic_7483_1_carry_out), .S4(ic_7483_1_s4), .S3(ic_7483_1_s3), .S2(ic_7483_1_s2),
    .S1(ic_7483_1_s1));  // open: VCC, GND
  IC_7432_OR ic_7432_or_1 (
    ._9(ic_7483_1_carry_out), ._10(ic_7432_or_1__11), ._12(ic_7408_and_1__6), ._13(ic_7408_and_1__3),
    ._8(Carry), ._11(ic_7432_or_1__11));  // open: VCC_14, _1, _2, _4, _5, GND_7, _3, _6
  IC_7408_AND ic_7408_and_1 (
    ._1(ic_7483_1_s4), ._2(ic_7483_1_s3), ._4(ic_7483_1_s4), ._5(ic_7483_1_s2), ._3(ic_7408_and_1__3),
    ._6(ic_7408_and_1__6));  // open: VCC_14, _9, _10, _12, _13, GND_7, _8, _11
  IC_7483 ic_7483_2 (
    .B1(in_10), .B4(in_10), .B3(Carry), .B2(Carry), .A4(ic_7483_1_s4), .A3(ic_7483_1_s3), .A2(ic_7483_1_s2),
    .A1(ic_7483_1_s1), .C(in_10), .S4(S4), .S3(S3), .S2(S2), .S1(S1));  // open: VCC, GND, Carry_Out

  // Notes on the sheet:
  //   Z4Z2+Z4Z3
  //   K
  //   Z4Z3
  //   Z4Z2
endmodule

module Experiment_2 (
  input  B8,
  input  B7,
  input  B6,
  input  B5,
  input  B4,
  input  B3,
  input  B2,
  input  B1,
  input  A8,
  input  A7,
  input  A6,
  input  A5,
  input  A4,
  input  A3,
  input  A2,
  input  A1,
  input  Carry_In,
  output Carry_Out,
  output S8,
  output S7,
  output S6,
  output S5,
  output S4,
  output S3,
  output S2,
  output S1
);

  wire ic_7483_1_carry_out;

  IC_7483 ic_7483_1 (
    .B1(B1), .B4(B4), .B3(B3), .B2(B2), .A4(A4), .A3(A3), .A2(A2), .A1(A1), .C(Carry_In),
    .Carry_Out(ic_7483_1_carry_out), .S4(S4), .S3(S3), .S2(S2), .S1(S1));  // open: VCC, GND
  IC_7483 ic_7483_2 (
    .B1(B5), .B4(B8), .B3(B7), .B2(B6), .A4(A8), .A3(A7), .A2(A6), .A1(A5), .C(ic_7483_1_carry_out),
    .Carry_Out(Carry_Out), .S4(S8), .S3(S7), .S2(S6), .S1(S5));  // open: VCC, GND
endmodule
