// Logisim project Nawal Ayesha_1911301042 Lab 6.circ as structural Verilog: 13 circuits, main circuit main
module main (
  input  in_1,
  input  in_2,
  input  in_3,
  output out_4
);

  Multiplexer #(.select(2), .enable("false")) multiplexer_1 (
    .in0(1'b1), .in1(1'b0), .in2(in_1), .in3(in_1), .out(out_4), .sel({in_2, in_3}));
endmodule

module IC_7404_NOT (
  input  GND_7,
  input  _1,
  input  _3,
  input  _5,
  input  _9,
  input  _11,
  input  _13,
  input  VCC_14,
  output _2,
  output _4,
  output _6,
  output _8,
  output _10,
  output _12
);

  not not_1 (_2, _1);
  not not_2 (_4, _3);
  not not_3 (_6, _5);
  not not_4 (_8, _9);
  not not_5 (_10, _11);
  not not_6 (_12, _13);
endmodule

module IC_7408_AND (
  input  VCC_14,
  input  _1,
  input  _2,
  input  _4,
  input  _5,
  input  _9,
  input  _10,
  input  _12,
  input  _13,
  input  GND_7,
  output _3,
  output _6,
  output _8,
  output _11
);

  and and_1 (_3, _1, _2);
  and and_2 (_6, _4, _5);
  and and_3 (_8, _9, _10);
  and and_4 (_11, _12, _13);
endmodule

module IC_7432_OR (
  input  VCC_14,
  input  _1,
  input  _2,
  input  _4,
  input  _5,
  input  _9,
  input  _10,
  input  _12,
  input  _13,
  input  GND_7,
  output _3,
  output _6,
  output _8,
  output _11
);

  or or_1 (_3, _1, _2);
  or or_2 (_6, _4, _5);
  or or_3 (_8, _9, _10);
  or or_4 (_11, _12, _13);
endmodule

module IC_4073_3_Input_AND (
  input  in_1,
  input  in_2,
  input  in_3,
  input  in_4,
  input  in_5,
  input  in_6,
  input  in_7,
  input  in_8,
  input  in_9,
  input  in_10,
  input  in_11,
  output out_12,
  output out_13,
  output out_14
);

  and and_1 (out_12, in_2, in_3, in_4);
  and and_2 (out_13, in_5, in_6, in_7);
  and and_3 (out_14, in_8, in_9, in_10);
endmodule

module IC_4075_3_Input_OR (
  input  in_1,
  input  in_2,
  input  in_3,
  input  in_4,
  input  in_5,
  input  in_6,
  input  in_7,
  input  in_8,
  input  in_9,
  input  in_10,
  input  in_11,
  output out_12,
  output out_13,
  output out_14
);

  or or_1 (out_12, in_2, in_3, in_4);
  or or_2 (out_13, in_5, in_6, in_7);
  or or_3 (out_14, in_8, in_9, in_10);
endmodule

module IC_7486_XOR (
  input  in_1,
  input  in_2,
  input  in_3,
  input  in_4,
  input  in_5,
  input  in_6,
  input  in_7,
  input  in_8,
  input  in_9,
  input  in_10,
  output out_11,
  output out_12,
  output out_13,
  output out_14
);

  xor xor_1 (out_11, in_2, in_3);
  xor xor_2 (out_12, in_4, in_5);
  xor xor_3 (out_13, in_6, in_7);
  xor xor_4 (out_14, in_8, in_9);
endmodule

module _3_to_8_Decoder (
  input  x,
  input  y,
  input  z,
  output D0,
  output D1,
  output D2,
  output D3,
  output D4,
  output D5,
  output D6,
  output D7
);

  wire ic_7404_not_1__2, ic_7404_not_1__4, ic_7404_not_1__6;

  IC_7404_NOT ic_7404_not_1 (
    ._1(z), ._3(y), ._5(x), ._2(ic_7404_not_1__2), ._4(ic_7404_not_1__4), ._6(ic_7404_not_1__6));  // open: GND_7, _9, _11, _13, VCC_14, _8, _10, _12
  IC_4073_3_Input_AND ic_4073_3_input_and_1 (
    .in_2(ic_7404_not_1__2), .in_3(ic_7404_not_1__4), .in_4(ic_7404_not_1__6), .in_5(ic_7404_not_1__6),
    .in_6(ic_7404_not_1__4), .in_7(z), .in_8(ic_7404_not_1__6), .in_9(y), .in_10(ic_7404_not_1__2),
    .out_12(D0), .out_13(D1), .out_14(D2));  // open: in_1, in_11
  IC_4073_3_Input_AND ic_4073_3_input_and_2 (
    .in_2(ic_7404_not_1__6), .in_3(y), .in_4(z), .in_5(x), .in_6(ic_7404_not_1__4), .in_7(ic_7404_not_1__2),
    .in_8(z), .in_9(ic_7404_not_1__4), .in_10(x), .out_12(D3), .out_13(D4), .out_14(D5));  // open: in_1, in_11
  IC_4073_3_Input_AND ic_4073_3_input_and_3 (
    .in_2(x), .in_3(y), .in_4(ic_7404_not_1__2), .in_5(y), .in_6(x), .in_7(z), .out_12(D6), .out_13(D7));  // open: in_1, in_8, in_9, in_10, in_11, out_14

  // Notes on the sheet:
  //   z'
  //   y'
  //   x'
  //   xyz'
  //   xyz
  //   x'y'z'
  //   x'y'z
  //   x'yz'
  //   xy'z
  //   x'yz
  //   xy'z'
endmodule

module _8_to_1_MUX (
  input  I0,
  input  I1,
  input  I2,
  input  I3,
  input  I4,
  input  I5,
  input  I6,
  input  I7,
  input  S0,
  input  S1,
  input  S2,
  output Y
);

  wire n4_1_mux_1_f, n4_1_mux_2_f;

  _4_1_MUX u_4_1_mux_1 (.F(n4_1_mux_1_f), .I3(I3), .I2(I2), .I1(I1), .I0(I0), .S1(S1), .S0(S0));
  _4_1_MUX u_4_1_mux_2 (.F(n4_1_mux_2_f), .I3(I7), .I2(I6), .I1(I5), .I0(I4), .S1(S1), .S0(S0));
  Multiplexer #(.enable("false")) multiplexer_1 (.in0(n4_1_mux_1_f), .in1(n4_1_mux_2_f), .out(Y), .sel(S2));
endmodule

module Experiment_1 (
  input  A,
  input  B,
  input  C,
  output F
);

  _4_1_MUX u_4_1_mux_1 (.F(F), .I3(C), .I2(C), .I1(1'b0), .I0(1'b1), .S1(A), .S0(B));
endmodule

module Experiment_2_D2 (
  input  A,
  input  B,
  input  C,
  input  D,
  output F
);

  _8_to_1_MUX u_8_to_1_mux_1 (
    .I0(1'b1), .I1(D), .I2(D), .I3(1'b0), .I4(1'b1), .I5(1'b0), .I6(1'b0), .I7(1'b1), .S0(C), .S1(B), .S2(A),
    .Y(F));
endmodule

module Experiment_2_E2 (
  input  A,
  input  B,
  input  C,
  input  D,
  output F
);

  wire ic_7404_not_1__2;

  IC_7404_NOT ic_7404_not_1 (
    ._1(D), ._2(ic_7404_not_1__2));  // open: GND_7, _3, _5, _9, _11, _13, VCC_14, _4, _6, _8, _10, _12
  _8_to_1_MUX u_8_to_1_mux_1 (
    .I0(D), .I1(ic_7404_not_1__2), .I2(1'b1), .I3(1'b0), .I4(1'b0), .I5(ic_7404_not_1__2), .I6(1'b1),
    .I7(1'b0), .S0(C), .S1(B), .S2(A), .Y(F));

  // Notes on the sheet:
  //   D'
  //   D
endmodule

module _4_1_MUX (
  input  I3,
  input  I2,
  input  I1,
  input  I0,
  input  S1,
  input  S0,
  output F
);

  wire and_1_out, and_2_out, and_3_out, and_4_out, not_1_out, not_2_out, or_1_out, or_2_out;

  not not_1 (not_1_out, S0);
  not not_2 (not_2_out, S1);
  and and_1 (and_1_out, I0, not_2_out, not_1_out);
  and and_2 (and_2_out, not_2_out, S0, I1);
  and and_3 (and_3_out, S1, not_1_out, I2);
  and and_4 (and_4_out, S0, S1, I3);
  or or_1 (or_1_out, and_1_out, and_2_out);
  or or_2 (or_2_out, and_3_out, and_4_out);
  or or_3 (F, or_1_out, or_2_out);
endmodule
