// Logisim project Nawal Ayesha_1911301042 Lab 7A.circ as structural Verilog: 10 circuits, main circuit main
module main (
  input  in_1,
  input  in_2,
  input  in_3,
  output out_4,
  output out_5,
  output out_6
);

  wire clock_1_out, clock_2_out;

  Clock clock_1 (.out(clock_1_out));
  IC_7474 ic_7474_1 (
    .in_2(in_1), .in_3(clock_1_out), .in_4(in_2), .out_9(out_5), .out_10(out_4));  // open: in_1, in_5, in_6, in_7, in_8, out_11, out_12
  Clock clock_2 (.out(clock_2_out));
  D_Flip_Flop d_flip_flop_1 (
    .in_3(in_3), .in_4(clock_2_out), .out_11(out_6));  // open: in_1, in_2, in_5, in_6, in_7, in_8, in_9, in_10, out_12, out_13, out_14
endmodule

module IC_7404_NOT (
  input  GND_7,
  input  _1,
  input  _3,
  input  _5,
  input  _9,
  input  _11,
  input  _13,
  input  VCC_14,
  output _2,
  output _4,
  output _6,
  output _8,
  output _10,
  output _12
);

  not not_1 (_2, _1);
  not not_2 (_4, _3);
  not not_3 (_6, _5);
  not not_4 (_8, _9);
  not not_5 (_10, _11);
  not not_6 (_12, _13);
endmodule

module IC_7408_AND (
  input  VCC_14,
  input  _1,
  input  _2,
  input  _4,
  input  _5,
  input  _9,
  input  _10,
  input  _12,
  input  _13,
  input  GND_7,
  output _3,
  output _6,
  output _8,
  output _11
);

  and and_1 (_3, _1, _2);
  and and_2 (_6, _4, _5);
  and and_3 (_8, _9, _10);
  and and_4 (_11, _12, _13);
endmodule

module IC_7400_NAND (
  input  VCC_14,
  input  _1,
  input  _2,
  input  _4,
  input  _5,
  input  _9,
  input  _10,
  input  _12,
  input  _13,
  input  GND_7,
  output _3,
  output _6,
  output _8,
  output _11
);

  nand nand_1 (_3, _1, _2);
  nand nand_2 (_6, _4, _5);
  nand nand_3 (_8, _9, _10);
  nand nand_4 (_11, _12, _13);
endmodule

module IC_4073_3_Input_AND (
  input  in_1,
  input  in_2,
  input  in_3,
  input  in_4,
  input  in_5,
  input  in_6,
  input  in_7,
  input  in_8,
  input  in_9,
  input  in_10,
  input  in_11,
  output out_12,
  output out_13,
  output out_14
);

  and and_1 (out_12, in_2, in_3, in_4);
  and and_2 (out_13, in_5, in_6, in_7);
  and and_3 (out_14, in_8, in_9, in_10);
endmodule

module D_Flip_Flop (
  input  in_1,
  input  in_2,
  input  in_3,
  input  in_4,
  input  in_5,
  input  in_6,
  input  in_7,
  input  in_8,
  input  in_9,
  input  in_10,
  output out_11,
  output out_12,
  output out_13,
  output out_14
);

  D_Flip_Flop_part d_ff_1 (.clk(in_4), .D(in_3), .Q(out_11), .Qn(out_12), .preset(in_5), .en(1'b1), .reset(in_2));
  D_Flip_Flop_part d_ff_2 (.clk(in_7), .D(in_8), .Q(out_13), .Qn(out_14), .preset(in_6), .en(1'b1), .reset(in_9));
endmodule

module IC_7474 (
  input  in_1,
  input  in_2,
  input  in_3,
  input  in_4,
  input  in_5,
  input  in_6,
  input  in_7,
  input  in_8,
  output out_9,
  output out_10,
  output out_11,
  output out_12
);

  J_K_Flip_Flop j_k_ff_1 (.J(in_2), .clk(in_3), .K(in_4), .Q(out_9), .Qn(out_10));  // open: preset, en, reset
  J_K_Flip_Flop j_k_ff_2 (.J(in_5), .clk(in_6), .K(in_7), .Q(out_11), .Qn(out_12));  // open: preset, en, reset
endmodule

module Experiment_3 (
  input  Serial_Input,
  output out_2,
  output Serial_Output,
  output out_4,
  output out_5
);

  wire Clock_out;

  Clock Clock (.out(Clock_out));
  D_Flip_Flop d_flip_flop_1 (
    .in_3(Serial_Input), .in_4(Clock_out), .in_7(Clock_out), .in_8(out_5), .out_11(out_5), .out_13(out_2));  // open: in_1, in_2, in_5, in_6, in_9, in_10, out_12, out_14
  D_Flip_Flop d_flip_flop_2 (
    .in_3(out_2), .in_4(Clock_out), .in_7(Clock_out), .in_8(out_4), .out_11(out_4), .out_13(Serial_Output));  // open: in_1, in_2, in_5, in_6, in_9, in_10, out_12, out_14
endmodule

module Experiment_2 (
  input  D,
  input  T,
  output out_3,
  output out_4,
  output out_5,
  output out_6
);

  wire CLK_out, clock_1_out, not_1_out;

  Clock clock_1 (.out(clock_1_out));
  not not_1 (not_1_out, D);
  IC_7474 ic_7474_1 (
    .in_2(not_1_out), .in_3(clock_1_out), .in_4(D), .out_9(out_5), .out_10(out_3));  // open: in_1, in_5, in_6, in_7, in_8, out_11, out_12
  Clock CLK (.out(CLK_out));
  IC_7474 ic_7474_2 (
    .in_2(T), .in_3(CLK_out), .in_4(T), .out_9(out_6), .out_10(out_4));  // open: in_1, in_5, in_6, in_7, in_8, out_11, out_12

  // Notes on the sheet:
  //   CLK
  //   D Flip-flop using JK-flip flop
  //   T Flip-flop using JK-flip flop
endmodule

module Experiment_1 (
  input  J,
  input  Preset,
  input  K,
  output out_4,
  output out_5
);

  wire and_1_out, and_2_out, and_3_out, and_4_out, Clear_out, clock_1_out, nor_1_out, nor_2_out, not_1_out,
       or_1_out, or_2_out;

  or or_1 (or_1_out, J, Preset);
  or or_2 (or_2_out, Preset, K);
  Clock clock_1 (.out(clock_1_out));
  and and_1 (and_1_out, out_5, or_1_out, clock_1_out);
  and and_2 (and_2_out, clock_1_out, or_2_out, out_4);
  not not_1 (not_1_out, clock_1_out);
  Button Clear (.out(Clear_out));
  nor nor_1 (nor_1_out, and_1_out, nor_2_out);
  nor nor_2 (nor_2_out, nor_1_out, and_2_out, Clear_out);
  and and_3 (and_3_out, not_1_out, nor_1_out);
  and and_4 (and_4_out, nor_2_out, not_1_out);
  nor nor_3 (out_4, and_3_out, out_5);
  nor nor_4 (out_5, out_4, and_4_out);
endmodule
