// Logisim project Nawal Ayesha_1911301042 Lab 7B.circ as structural Verilog: 2 circuits, main circuit main
module main (
  input  A,
  input  B,
  input  C,
  input  D
);

  wire ic_7447_1_a_2, ic_7447_1_b_2, ic_7447_1_c_2, ic_7447_1_d_2, ic_7447_1_e, ic_7447_1_f, ic_7447_1_g;

  IC_7447 ic_7447_1 (
    .A(A), .B(B), .C(C), .D(D), .a_2(ic_7447_1_a_2), .b_2(ic_7447_1_b_2), .c_2(ic_7447_1_c_2),
    .d_2(ic_7447_1_d_2), .e(ic_7447_1_e), .f(ic_7447_1_f), .g(ic_7447_1_g));  // open: GND, VCC
  _7_Segment_Display u_7_segment_display_1 (
    .g(ic_7447_1_g), .f(ic_7447_1_f), .a(ic_7447_1_a_2), .b(ic_7447_1_b_2), .e(ic_7447_1_e),
    .d(ic_7447_1_d_2), .c(ic_7447_1_c_2));  // open: dp
endmodule

module IC_7447 (
  input  GND,
  input  A,
  input  B,
  input  C,
  input  D,
  input  VCC,
  output a_2,
  output b_2,
  output c_2,
  output d_2,
  output e,
  output f,
  output g
);

  wire and_1_out, and_2_out, and_3_out, and_4_out, and_5_out, and_6_out, and_7_out, and_8_out, and_9_out,
       and_10_out, and_11_out, and_12_out, and_13_out, and_14_out, and_15_out, and_16_out, and_17_out,
       and_18_out, and_19_out, and_20_out, and_21_out, and_22_out, and_23_out, and_24_out, and_25_out,
       and_26_out, and_27_out, and_28_out, and_29_out, and_30_out, and_31_out, not_1_out, not_2_out,
       not_3_out, not_4_out, not_5_out, not_6_out, not_7_out, not_8_out, not_9_out, not_10_out, not_11_out,
       not_12_out, not_13_out, xnor_1_out, xor_1_out;

  not not_1 (not_1_out, C);
  not not_2 (not_2_out, A);
  not not_3 (not_3_out, D);
  not not_4 (not_4_out, B);
  not not_5 (not_5_out, A);
  not not_6 (not_6_out, A);
  not not_7 (not_7_out, B);
  not not_8 (not_8_out, D);
  not not_9 (not_9_out, C);
  not not_10 (not_10_out, D);
  xor xor_1 (xor_1_out, A, B);
  and and_1 (and_1_out, not_1_out, D);
  and and_2 (and_2_out, not_1_out, not_2_out);
  and and_3 (and_3_out, not_2_out, D);
  xnor xnor_1 (xnor_1_out, C, D);
  and and_4 (and_4_out, C, not_3_out);
  not not_11 (not_11_out, B);
  not not_12 (not_12_out, A);
  not not_13 (not_13_out, C);
  and and_5 (and_5_out, not_6_out, not_7_out, C);
  and and_6 (and_6_out, B, C, not_8_out);
  and and_7 (and_7_out, B, not_9_out, D);
  and and_8 (and_8_out, A, not_7_out, D);
  and and_9 (and_9_out, not_7_out, not_8_out, not_9_out);
  and and_10 (and_10_out, A, not_9_out);
  or or_1 (c_2, xor_1_out, and_1_out, and_2_out, and_3_out);
  and and_11 (and_11_out, A, xnor_1_out);
  and and_12 (and_12_out, B, A);
  and and_13 (and_13_out, not_3_out, not_4_out);
  and and_14 (and_14_out, A, not_4_out);
  and and_15 (and_15_out, C, A);
  and and_16 (and_16_out, not_3_out, B);
  and and_17 (and_17_out, not_1_out, not_3_out);
  and and_18 (and_18_out, not_5_out, B, not_1_out);
  and and_19 (and_19_out, not_4_out, C);
  and and_20 (and_20_out, not_3_out, and_4_out);
  and and_21 (and_21_out, D, A);
  and and_22 (and_22_out, not_11_out, not_12_out);
  and and_23 (and_23_out, not_11_out, not_10_out);
  and and_24 (and_24_out, not_12_out, C, D);
  and and_25 (and_25_out, D, not_13_out, A);
  and and_26 (and_26_out, not_12_out, not_13_out, not_10_out);
  and and_27 (and_27_out, not_12_out, C);
  and and_28 (and_28_out, not_10_out, A);
  and and_29 (and_29_out, C, B);
  and and_30 (and_30_out, not_12_out, B, D);
  and and_31 (and_31_out, not_13_out, not_11_out, A);
  or or_2 (e, and_11_out, and_4_out, and_12_out, and_13_out);
  or or_3 (f, and_14_out, and_15_out, and_16_out, and_17_out, and_18_out);
  or or_4 (d_2, and_5_out, and_6_out, and_9_out, and_7_out, and_8_out, and_10_out);
  or or_5 (g, and_18_out, and_14_out, and_19_out, and_20_out, and_21_out);
  or or_6 (b_2, and_23_out, and_22_out, and_24_out, and_26_out, and_25_out);
  or or_7 (a_2, and_23_out, and_27_out, and_20_out, and_28_out, and_29_out, and_30_out, and_31_out);

  // Notes on the sheet:
  //   A^B
  //   C'D
  //   A'C'
  //   A'D
  //   CD'
  //   A'B'C
  //   BCD'
  //   AB'D
  //   B'C'D'
  //   AC'
  //   A(C^D)'
  //   AB
  //   B'D'
  //   AB'
  //   AC
  //   BD'
  //   C'D'
  //   A'BC'
  //   B'C
  //   CD'
  //   AD
  //   BC'D
  //   A'B'
  //   B'D'
  //   A'CD
  //   AC'D
  //   A'C'D'
  //   A'C
  //   CD'
  //   AD'
  //   BC
  //   A'BD
  //   AB'C'
  //   c
  //   e
  //   B'D'
  //   f
  //   g
  //   d
  //   b
  //   a
endmodule
