// Logisim project Nawal Ayesha_1911301042 Lab 8.circ as structural Verilog
module IC_7404_NOT (
  input  GND_7,
  input  _1,
  input  _3,
  input  _5,
  input  _9,
  input  _11,
  input  _13,
  input  VCC_14,
  output _2,
  output _4,
  output _6,
  output _8,
  output _10,
  output _12
);

  not not_1 (_2, _1);
  not not_2 (_4, _3);
  not not_3 (_6, _5);
  not not_4 (_8, _9);
  not not_5 (_10, _11);
  not not_6 (_12, _13);
endmodule

module IC_7408_AND (
  input  VCC_14,
  input  _1,
  input  _2,
  input  _4,
  input  _5,
  input  _9,
  input  _10,
  input  _12,
  input  _13,
  input  GND_7,
  output _3,
  output _6,
  output _8,
  output _11
);

  and and_1 (_3, _1, _2);
  and and_2 (_6, _4, _5);
  and and_3 (_8, _9, _10);
  and and_4 (_11, _12, _13);
endmodule

module D_Flip_Flop (
  input  in_1,
  input  in_2,
  input  in_3,
  input  in_4,
  input  in_5,
  input  in_6,
  input  in_7,
  input  in_8,
  output out_9,
  output out_10,
  output out_11,
  output out_12
);

  D_Flip_Flop_part d_ff_1 (.clk(in_4), .D(in_3), .Q(out_9), .Qn(out_10), .preset(in_5), .en(1'b1), .reset(in_2));
  D_Flip_Flop_part d_ff_2 (.clk(in_6), .D(in_7), .Q(out_11), .Qn(out_12), .preset(in_5), .en(1'b1), .reset(in_2));
endmodule

module IC_7474 (
  input  in_1,
  input  in_2,
  input  in_3,
  input  in_4,
  input  in_5,
  input  in_6,
  input  in_7,
  input  in_8,
  input  CLR,
  input  PR,
  output out_11,
  output out_12,
  output out_13,
  output out_14
);

  J_K_Flip_Flop j_k_ff_1 (.J(in_2), .clk(in_3), .K(in_4), .Q(out_11), .Qn(out_12), .preset(CLR), .en(1'b1), .reset(PR));
  J_K_Flip_Flop j_k_ff_2 (.J(in_5), .clk(in_6), .K(in_7), .Q(out_13), .Qn(out_14), .preset(CLR), .en(1'b1), .reset(PR));
endmodule

module Experiment_2 (
  input  X,
  input  Preset,
  input  Clear,
  output A,
  output B,
  output Y
);

  wire and_1_out, and_2_out, Clock_out, not_1_out, or_1_out, t_ff_1_qn, t_ff_2_qn;

  Clock Clock (.out(Clock_out));
  not not_1 (not_1_out, X);
  and and_1 (and_1_out, t_ff_1_qn, t_ff_2_qn, not_1_out);
  and and_2 (and_2_out, X, B);
  or or_1 (or_1_out, and_1_out, and_2_out);
  T_Flip_Flop_part t_ff_1 (.clk(Clock_out), .T(X), .Q(A), .Qn(t_ff_1_qn), .preset(Preset), .reset(Clear));  // open: en
  T_Flip_Flop_part t_ff_2 (
    .clk(Clock_out), .T(or_1_out), .Q(B), .Qn(t_ff_2_qn), .preset(Preset), .reset(Clear));  // open: en
  and and_3 (Y, t_ff_1_qn, X);

  // Notes on the sheet:
  //   A'B'X'
  //   BX
  //   A'X
endmodule

module Experiment_3 (
  input  x,
  input  Preset,
  input  Clear,
  output A,
  output B,
  output y
);

  wire and_1_out, and_2_out, and_3_out, Clock_out, d_ff_1_qn, not_1_out, or_1_out;

  not not_1 (not_1_out, x);
  Clock Clock (.out(Clock_out));
  and and_1 (and_1_out, A, not_1_out);
  and and_2 (and_2_out, x, d_ff_1_qn);
  or or_1 (or_1_out, and_1_out, and_2_out);
  and and_3 (and_3_out, d_ff_1_qn, not_1_out);
  and and_4 (y, x, d_ff_1_qn);
  D_Flip_Flop_part d_ff_1 (
    .clk(Clock_out), .D(or_1_out), .Q(A), .Qn(d_ff_1_qn), .preset(Preset), .reset(Clear));  // open: en
  D_Flip_Flop_part d_ff_2 (.clk(Clock_out), .D(and_3_out), .Q(B), .preset(Preset), .reset(Clear));  // open: Qn, en

  // Notes on the sheet:
  //   A'X'
  //   AX'+A'X
  //   A'X
  //   A'x'
endmodule

module Experiment_1_IC (
  input  X,
  input  Preset,
  output A,
  output B,
  output Y
);

  wire and_1_out, Clear_out, Clock_out, ic_7474_1_out_12, not_1_out;

  Clock Clock (.out(Clock_out));
  Button Clear (.out(Clear_out));
  not not_1 (not_1_out, X);
  and and_1 (and_1_out, ic_7474_1_out_12, not_1_out);
  IC_7474 ic_7474_1 (
    .in_2(X), .in_3(Clock_out), .in_4(X), .in_5(and_1_out), .in_6(Clock_out), .in_7(X), .out_11(A),
    .out_12(ic_7474_1_out_12), .out_13(B), .CLR(Clear_out), .PR(Preset));  // open: in_1, in_8, out_14
  and and_2 (Y, ic_7474_1_out_12, X);

  // Notes on the sheet:
  //   A'X'
  //   A'X
endmodule

module Experiment_2_IC (
  input  X,
  input  Preset,
  output A,
  output B,
  output Y
);

  wire and_1_out, and_2_out, Clock_out, CLR_out, not_1_out, or_1_out, t_flip_flop_1_out_6,
       t_flip_flop_2_out_6;

  Clock Clock (.out(Clock_out));
  Button CLR (.out(CLR_out));
  not not_1 (not_1_out, X);
  and and_1 (and_1_out, not_1_out, t_flip_flop_1_out_6, t_flip_flop_2_out_6);
  and and_2 (and_2_out, X, B);
  and and_3 (Y, t_flip_flop_1_out_6, X);
  or or_1 (or_1_out, and_1_out, and_2_out);
  T_Flip_Flop t_flip_flop_1 (
    .in_1(CLR_out), .in_2(X), .in_3(Clock_out), .in_4(Preset), .out_5(A), .out_6(t_flip_flop_1_out_6));
  T_Flip_Flop t_flip_flop_2 (
    .in_1(CLR_out), .in_2(or_1_out), .in_3(Clock_out), .in_4(Preset), .out_5(B), .out_6(t_flip_flop_2_out_6));

  // Notes on the sheet:
  //   A'B'X'
  //   BX
  //   A'X
endmodule

module T_Flip_Flop (
  input  in_1,
  input  in_2,
  input  in_3,
  input  in_4,
  output out_5,
  output out_6
);

  T_Flip_Flop_part t_ff_1 (.clk(in_3), .T(in_2), .Q(out_5), .Qn(out_6), .preset(in_4), .reset(in_1), .en(1'b1));
endmodule

module Experiment_3_IC (
  input  X,
  input  Preset,
  output A,
  output B,
  output Y
);

  wire Clear_out, Clock_out, d_flip_flop_1_out_10, ic_7404_not_1__12, ic_7408_and_1__3, ic_7408_and_1__11,
       ic_7432_1__3;

  Clock Clock (.out(Clock_out));
  Button Clear (.out(Clear_out));
  D_Flip_Flop d_flip_flop_1 (
    .in_2(Clear_out), .in_3(ic_7432_1__3), .in_4(Clock_out), .in_5(Preset), .in_6(Clock_out),
    .in_7(ic_7408_and_1__11), .out_9(A), .out_10(d_flip_flop_1_out_10), .out_11(B));  // open: in_1, in_8, out_12
  IC_7404_NOT ic_7404_not_1 (
    ._13(X), ._12(ic_7404_not_1__12));  // open: GND_7, _1, _3, _5, _9, _11, VCC_14, _2, _4, _6, _8, _10
  IC_7432 ic_7432_1 (
    ._1(ic_7408_and_1__3), ._2(Y), ._3(ic_7432_1__3));  // open: VCC_14, _4, _5, _9, _10, _12, _13, GND_7, _6, _8, _11
  IC_7408_AND ic_7408_and_1 (
    ._1(ic_7404_not_1__12), ._2(A), ._4(X), ._5(d_flip_flop_1_out_10), ._12(d_flip_flop_1_out_10),
    ._13(ic_7404_not_1__12), ._3(ic_7408_and_1__3), ._6(Y), ._11(ic_7408_and_1__11));  // open: VCC_14, _9, _10, GND_7, _8

  // Notes on the sheet:
  //   A'X+AX'
  //   A'X'
  //   X'
  //   AX'
  //   A'X
  //   A'X+AX'
  //   A'X'
endmodule

module IC_7432 (
  input  VCC_14,
  input  _1,
  input  _2,
  input  _4,
  input  _5,
  input  _9,
  input  _10,
  input  _12,
  input  _13,
  input  GND_7,
  output _3,
  output _6,
  output _8,
  output _11
);

  or or_1 (_3, _1, _2);
  or or_2 (_6, _4, _5);
  or or_3 (_8, _9, _10);
  or or_4 (_11, _12, _13);
endmodule
