// Logisim project Nawal Ayesha_1911301042 Mid.circ as structural Verilog
module IC_7404_NOT (
  input  GND_7,
  input  _1,
  input  _3,
  input  _5,
  input  _9,
  input  _11,
  input  _13,
  input  VCC_14,
  output _2,
  output _4,
  output _6,
  output _8,
  output _10,
  output _12
);

  not not_1 (_2, _1);
  not not_2 (_4, _3);
  not not_3 (_6, _5);
  not not_4 (_8, _9);
  not not_5 (_10, _11);
  not not_6 (_12, _13);
endmodule

module IC_7408_AND (
  input  VCC_14,
  input  _1,
  input  _2,
  input  _4,
  input  _5,
  input  _9,
  input  _10,
  input  _12,
  input  _13,
  input  GND_7,
  output _3,
  output _6,
  output _8,
  output _11
);

  and and_1 (_3, _1, _2);
  and and_2 (_6, _4, _5);
  and and_3 (_8, _9, _10);
  and and_4 (_11, _12, _13);
endmodule

module IC_7432_OR (
  input  VCC_14,
  input  _1,
  input  _2,
  input  _4,
  input  _5,
  input  _9,
  input  _10,
  input  _12,
  input  _13,
  input  GND_7,
  output _3,
  output _6,
  output _8,
  output _11
);

  or or_1 (_3, _1, _2);
  or or_2 (_6, _4, _5);
  or or_3 (_8, _9, _10);
  or or_4 (_11, _12, _13);
endmodule

module IC_7400_NAND (
  input  VCC_14,
  input  _1,
  input  _2,
  input  _4,
  input  _5,
  input  _9,
  input  _10,
  input  _12,
  input  _13,
  input  GND_7,
  output _3,
  output _6,
  output _8,
  output _11
);

  nand nand_1 (_3, _1, _2);
  nand nand_2 (_6, _4, _5);
  nand nand_3 (_8, _9, _10);
  nand nand_4 (_11, _12, _13);
endmodule

module IC_4073_3_Input_AND (
  input  in_1,
  input  in_2,
  input  in_3,
  input  in_4,
  input  in_5,
  input  in_6,
  input  in_7,
  input  in_8,
  input  in_9,
  input  in_10,
  input  in_11,
  output out_12,
  output out_13,
  output out_14
);

  and and_1 (out_12, in_2, in_3, in_4);
  and and_2 (out_13, in_5, in_6, in_7);
  and and_3 (out_14, in_8, in_9, in_10);
endmodule

module IC_4075_3_Input_OR (
  input  in_1,
  input  in_2,
  input  in_3,
  input  in_4,
  input  in_5,
  input  in_6,
  input  in_7,
  input  in_8,
  input  in_9,
  input  in_10,
  input  in_11,
  output out_12,
  output out_13,
  output out_14
);

  or or_1 (out_12, in_2, in_3, in_4);
  or or_2 (out_13, in_5, in_6, in_7);
  or or_3 (out_14, in_8, in_9, in_10);
endmodule

module IC_7402_NOR (
  input  VCC_14,
  input  _1,
  input  _2,
  input  _4,
  input  _5,
  input  _9,
  input  _10,
  input  _12,
  input  _13,
  input  GND_7,
  output _3,
  output _6,
  output _8,
  output _11
);

  nor nor_1 (_3, _1, _2);
  nor nor_2 (_6, _4, _5);
  nor nor_3 (_8, _9, _10);
  nor nor_4 (_11, _12, _13);
endmodule

module IC_7486_XOR (
  input  in_1,
  input  in_2,
  input  in_3,
  input  in_4,
  input  in_5,
  input  in_6,
  input  in_7,
  input  in_8,
  input  in_9,
  input  in_10,
  output out_11,
  output out_12,
  output out_13,
  output out_14
);

  xor xor_1 (out_11, in_2, in_3);
  xor xor_2 (out_12, in_4, in_5);
  xor xor_3 (out_13, in_6, in_7);
  xor xor_4 (out_14, in_8, in_9);
endmodule

module IC_7483_4_bit_Adder (
  input  VCC,
  input  GND,
  input  A4,
  input  A3,
  input  A2,
  input  A1,
  input  C,
  input  B1,
  input  B4,
  input  B3,
  input  B2,
  output Carry_Out,
  output S4,
  output S3,
  output S2,
  output S1
);

  wire and_1_out, and_2_out, and_3_out, and_4_out, and_5_out, and_6_out, and_7_out, and_8_out, or_2_out,
       or_3_out, or_4_out, xor_1_out, xor_2_out, xor_3_out, xor_4_out;

  xor xor_1 (xor_1_out, A1, B1);
  and and_1 (and_1_out, A1, B1);
  xor xor_2 (xor_2_out, A4, B4);
  and and_2 (and_2_out, A4, B4);
  xor xor_3 (xor_3_out, A2, B2);
  and and_3 (and_3_out, A2, B2);
  xor xor_4 (xor_4_out, A3, B3);
  and and_4 (and_4_out, A3, B3);
  xor xor_5 (S1, xor_1_out, C);
  and and_5 (and_5_out, xor_1_out, C);
  xor xor_6 (S4, xor_2_out, or_4_out);
  and and_6 (and_6_out, xor_2_out, or_4_out);
  xor xor_7 (S2, xor_3_out, or_2_out);
  and and_7 (and_7_out, xor_3_out, or_2_out);
  xor xor_8 (S3, xor_4_out, or_3_out);
  and and_8 (and_8_out, xor_4_out, or_3_out);
  or or_1 (Carry_Out, and_6_out, and_2_out);
  or or_2 (or_2_out, and_5_out, and_1_out);
  or or_3 (or_3_out, and_7_out, and_3_out);
  or or_4 (or_4_out, and_8_out, and_4_out);

  // Notes on the sheet:
  //   C1
  //   C2
endmodule

module Question_2_a (
  input  A,
  input  B,
  input  C,
  output X,
  output Y,
  output Z
);

  wire ic_7404_not_1__2, ic_7404_not_1__6, ic_7408_and_1__3, ic_7486_xor_1_out_11, ic_7486_xor_1_out_12;

  IC_7408_AND ic_7408_and_1 (
    ._1(C), ._2(A), ._4(ic_7404_not_1__6), ._5(C), ._3(ic_7408_and_1__3), ._6(Z));  // open: VCC_14, _9, _10, _12, _13, GND_7, _8, _11
  IC_7404_NOT ic_7404_not_1 (
    ._1(ic_7408_and_1__3), ._5(B), ._2(ic_7404_not_1__2), ._6(ic_7404_not_1__6));  // open: GND_7, _3, _9, _11, _13, VCC_14, _4, _8, _10, _12
  IC_7486_XOR ic_7486_xor_1 (
    .in_2(ic_7404_not_1__2), .in_3(B), .in_4(ic_7408_and_1__3), .in_5(C), .out_11(ic_7486_xor_1_out_11),
    .out_12(ic_7486_xor_1_out_12));  // open: in_1, in_6, in_7, in_8, in_9, in_10, out_13, out_14
  IC_7432_OR ic_7432_or_1 (
    ._1(A), ._2(ic_7486_xor_1_out_11), ._4(ic_7486_xor_1_out_12), ._5(A), ._3(X), ._6(Y));  // open: VCC_14, _9, _10, _12, _13, GND_7, _8, _11

  // Notes on the sheet:
  //   AC
  //   B'C
  //   (AC)' XOR B
  //   AC XOR C
  //   (AC)'
  //   B'
  //   ACB'+(AC)'B+A
  //   (AC)'C+(AC)C'+A
  //   B'C
endmodule

module Question_2_b_IC_7411 (
  input  in_1,
  input  in_2,
  input  in_3,
  input  in_4,
  input  in_5,
  input  in_6,
  input  in_7,
  input  in_8,
  input  in_9,
  input  in_10,
  input  in_11,
  output out_12,
  output out_13,
  output out_14
);

  and and_1 (out_12, in_2, in_3, in_4);
  and and_2 (out_13, in_5, in_6, in_7);
  and and_3 (out_14, in_8, in_9, in_10);
endmodule

module Question_1_b (
  input  A,
  input  B,
  input  C,
  output Y,
  output X
);

  wire and_1_out, and_2_out, and_3_out, and_4_out, and_5_out, and_6_out, not_1_out, not_2_out, or_2_out;

  not not_1 (not_1_out, A);
  not not_2 (not_2_out, B);
  and and_1 (and_1_out, A, B);
  and and_2 (and_2_out, C, B);
  and and_3 (and_3_out, C, A);
  and and_4 (and_4_out, B, not_1_out);
  and and_5 (and_5_out, A, not_2_out);
  and and_6 (and_6_out, not_1_out, C);
  or or_1 (Y, and_1_out, and_2_out, and_3_out);
  or or_2 (or_2_out, and_4_out, and_5_out);
  or or_3 (X, and_3_out, or_2_out, and_6_out);

  // Notes on the sheet:
  //   AB
  //   BC
  //   AC
  //   A'B
  //   AB'
  //   A'C
endmodule

module Bonus_question_IC_7408 (
  input  VCC_14,
  input  _1,
  input  _2,
  input  _4,
  input  _5,
  input  _9,
  input  _10,
  input  _12,
  input  _13,
  input  GND_7,
  output _3,
  output _6,
  output _8,
  output _11
);

  and and_1 (_3, _1, _2);
  and and_2 (_6, _4, _5);
  and and_3 (_8, _9, _10);
  and and_4 (_11, _12, _13);
endmodule
